# Fritzing sketch game controller (saved by Fritzing 0.9.3b)
breadboards: 1

parts:
  Part1 = Arduino Uno (Rev3) - ICSP
  U1 = POT_SWITCH [package=pot_pth]
  U2 = POT_SWITCH [package=pot_pth]

nets:
  N1: Part1.A0, U2.G$2_1
  N2: Part1.A1, U1.G$2_1
  N3: Part1.GND, U1.G$1_A, U2.G$1_A
  N4: Part1.5V, U1.G$1_E, U2.G$1_E
